# Fritzing sketch schematics (saved by Fritzing 1.0.4)

parts:
  A1 = ESP32 DevKitc V4
  LCD1 = LCD screen
  S3 = SWITCH-MOMENTARY-2 [package=tactile-switch-1101ne]
  S1 = SWITCH-MOMENTARY-2 [package=tactile-switch-1101ne]
  S4 = SWITCH-MOMENTARY-2 [package=tactile-switch-1101ne]
  S2 = SWITCH-MOMENTARY-2 [package=tactile-switch-1101ne]
  LCM1602_IIC1 = LCM1602 IIC [part_number="LCM1602 IIC" chip_label="LCM1602 IIC" package="DIP (Dual Inline) [THT]"]

nets:
  N1: A1.Pin_3, S1.1
  N2: A1.Pin_4, S2.1
  N3: A1.Pin_5, S3.1
  N4: A1.Pin_6, S4.1
  N5: A1.Pin_7, LCM1602_IIC1.LED_A
  N6: A1.Pin_18, S3.2, S1.2, S4.2, S2.2, LCM1602_IIC1.GND
  N7: A1.Pin_19, LCM1602_IIC1.VCC
  N8: A1.Pin_33, LCM1602_IIC1.SDA
  N9: A1.Pin_36, LCM1602_IIC1.SCL
  VSS: LCD1.VSS, LCM1602_IIC1.VSS
  VDD: LCD1.VDD, LCM1602_IIC1.VDD
  N10: LCD1.V0, LCM1602_IIC1.V0
  N11: LCD1.RS, LCM1602_IIC1.RS
  N12: LCD1.R/W, LCM1602_IIC1.RW
  N13: LCD1.E, LCM1602_IIC1.E
  N14: LCD1.DB0, LCM1602_IIC1.D0
  N15: LCD1.DB1, LCM1602_IIC1.D1
  N16: LCD1.DB2, LCM1602_IIC1.D2
  N17: LCD1.DB3, LCM1602_IIC1.D3
  N18: LCD1.DB4, LCM1602_IIC1.D4
  N19: LCD1.DB5, LCM1602_IIC1.D5
  N20: LCD1.DB6, LCM1602_IIC1.D6
  N21: LCD1.DB7, LCM1602_IIC1.D7
  N22: LCD1.LED+, LCM1602_IIC1.A
  N23: LCD1.LED-, LCM1602_IIC1.K

notes:
  Take out jumper in LCM1602 and use upper connector (LED+/Anode)
  Current configuration is using internal pullups for switches on GPIO

custom parts:
  ESP32 DevKitc V4: ESP32-DevKitC board with ESP32-WROOM-32 module. ESP32-DevKitC V4 is a small-sized ESP32-based development board produced by Espressif. Most of the pins on the ESP module are broken out to the pin headers on the board. The pins D0, D1, D2, D3, CMD and CLK are used internally for communication between ESP32 and SPI flash memory. They are grouped on both sides near the USB connector. Avoid using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
  LCM1602 IIC: I2C-Module to use a 1602 or 2004 LCD on with the wire.h libory Serial LCD Modul
